# Fritzing sketch schem (saved by Fritzing 0.9.10b)
breadboards: 1

parts:
  Part1 = Arduino Uno (Rev3)
  M1 = Stepper Motor - Bipolar
  M2 = Stepper Motor - Bipolar
  Pololu_A2 = Pololu A4988 [package=SO16]
  Pololu_A3 = Pololu A4988 [package=SO16]
  C1 = Electrolytic Capacitor [capacitance=47µF voltage=35V package="100 mil [THT, electrolytic]"]
  C2 = Electrolytic Capacitor [capacitance=47µF voltage=35V package="100 mil [THT, electrolytic]"]
  Mod1 = YL-99 Limit switch and LED
  Mod2 = YL-99 Limit switch and LED
  J1 = Basic Servo
  J2 = Basic Servo

nets:
  N1: Part1.D9_PWM, J2.pulse
  N2: Part1.D10_PWM/SS, J1.pulse
  N3: Part1.D11_PWM/MOSI, Mod2.OUT
  N4: Part1.D3_PWM, Mod1.OUT
  N5: Part1.D4, Pololu_A2.STEP
  N6: Part1.D5_PWM, Pololu_A2.DIR
  N7: Part1.D6_PWM, Pololu_A3.STEP
  N8: Part1.D7, Pololu_A3.DIR
  VDD: Part1.5V, Pololu_A2.VDD, Pololu_A3.VDD, J1.vcc, J2.vcc
  GND: Part1.GND, Pololu_A2.GND, Pololu_A3.GND, C1.-, C2.-, Mod1.GND, Mod2.GND, J1.gnd, J2.gnd
  N9: Part1.VIN, Pololu_A2.VMOT, Pololu_A3.VMOT, C1.+, C2.+
  N10: M1.A, Pololu_A2.2B
  N11: M1.C, Pololu_A2.2A
  N12: M1.B, Pololu_A2.1A
  N13: M1.D, Pololu_A2.1B
  N14: M2.A, Pololu_A3.2B
  N15: M2.C, Pololu_A3.2A
  N16: M2.B, Pololu_A3.1A
  N17: M2.D, Pololu_A3.1B
  N18: Pololu_A2.RESET, Pololu_A2.SLEEP
  N19: Pololu_A3.RESET, Pololu_A3.SLEEP

notes:
  12V
  5V
  Linear actuator servo
  Grabber servo
